# Fritzing sketch tbos (saved by Fritzing 0.9.5d)
breadboards: 1

parts:
  pyboard1 = Micro Python pyboard [part_number=PYBv10b]
  L298N1 = L298N DC motor driver

nets:
  N1: pyboard1.P9A_GND, L298N1.GND
  N2: pyboard1.X2, L298N1.ENA
  N3: pyboard1.X3, L298N1.IN2
  N4: pyboard1.X4, L298N1.IN1

custom parts:
  L298N DC motor driver: 2x DC motor driver with 78M05 positive voltage regulator (7..35 V) L298N: max 46 V, 2 A Set 5 V Enable jumper to enable 5 V regultor (needed for the L298N) and +5 V output at screw terminal or supply external +5 V at screw terminal Set ENA and/or ENB to +5 V to enable motor permanently or supply ENA and/or ENB with PWM signal IN1 and IN2 set rotation directory for motor A (OUT1/OUT2) IN2 and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
